# Fritzing sketch only_screen__QNG7huC6ng (saved by Fritzing 0.9.3b)

parts:
  ILI_9341 = ILI9341
  Part1 = Arduino Mega 2560 (Rev3)

nets:
  VCC: ILI_9341.VCC, Part1.5V
  GND: ILI_9341.GND, Part1.GND
  N1: ILI_9341.CS, Part1.D53
  N2: ILI_9341.RESET, Part1.D49
  N3: ILI_9341.DC, Part1.D48
  N4: ILI_9341.SDI(MOSI), Part1.D51
  N5: ILI_9341.SCK, Part1.D52
  N6: ILI_9341.LED, Part1.3V3
  N7: ILI_9341.SDO(MISO), Part1.D50

notes:
  2.8 ILI 9341

custom parts:
  ILI9341: ILI 9341
